// Digital circuit Clock Conversion.dig as structural Verilog
module Clock_Conversion (
  input  CLK_IN,
  input  A,
  input  B,
  output CLK_OUT
);

  wire jk_ff_1_q, jk_ff_2_q, jk_ff_3_q, jk_ff_4_q;
  wire [1:0] not_1_out;

  JK_FF jk_ff_1 (.J(1'b1), .C(CLK_IN), .K(1'b1), .Q(jk_ff_1_q));  // open: nQ
  JK_FF jk_ff_2 (.J(1'b1), .C(jk_ff_1_q), .K(1'b1), .Q(jk_ff_2_q));  // open: nQ
  JK_FF jk_ff_3 (.J(1'b1), .C(jk_ff_2_q), .K(1'b1), .Q(jk_ff_3_q));  // open: nQ
  JK_FF jk_ff_4 (.J(1'b1), .C(jk_ff_3_q), .K(1'b1), .Q(jk_ff_4_q));  // open: nQ
  Multiplexer #(.Selector_Bits(2)) multiplexer_1 (
    .sel(not_1_out), .in_0(jk_ff_1_q), .in_1(jk_ff_2_q), .in_2(jk_ff_3_q), .in_3(jk_ff_4_q), .out(CLK_OUT));
  not not_1 (not_1_out[0], A);
  not not_2 (not_1_out[1], B);

  // Notes on the sheet:
  //   B: default 1
endmodule
