// Digital circuit Enable Counter.dig as structural Verilog
module Enable_Counter (
  input  CLK,
  output DISP_EN
);

  wire and_1_out, not_1_out, not_2_out, not_3_out, t_ff_1_q, t_ff_2_q, t_ff_3_q;

  T_FF t_ff_1 (.T(1'b1), .C(CLK), .Q(t_ff_1_q));  // open: nQ
  T_FF t_ff_2 (.T(t_ff_1_q), .C(CLK), .Q(t_ff_2_q));  // open: nQ
  and and_1 (and_1_out, t_ff_1_q, t_ff_2_q);
  T_FF t_ff_3 (.T(and_1_out), .C(CLK), .Q(t_ff_3_q));  // open: nQ
  not not_1 (not_1_out, t_ff_1_q);
  not not_2 (not_2_out, t_ff_2_q);
  not not_3 (not_3_out, t_ff_3_q);
  and and_2 (DISP_EN, not_1_out, not_2_out, not_3_out);
endmodule
