// Digital circuit Full Circuit.dig as structural Verilog
module Full_Circuit (
  input  A,
  input  B,
  input  CLK_IN,
  input  START,
  input  SERIAL,
  output [15:0] OUT
);

  wire clock_conversion_1_clk_out, serial_to_parallel_data_1_disp_en;
  wire [15:0] serial_to_parallel_data_1_parallel_out;

  Clock_Conversion clock_conversion_1 (.CLK_IN(CLK_IN), .A(A), .B(B), .CLK_OUT(clock_conversion_1_clk_out));
  serial_to_parallel_data serial_to_parallel_data_1 (
    .START(START), .CLK(clock_conversion_1_clk_out), .SERIAL_IN(SERIAL),
    .PARALLEL_OUT(serial_to_parallel_data_1_parallel_out), .DISP_EN(serial_to_parallel_data_1_disp_en));
  display_buffer display_buffer_1 (
    .ENABLE(serial_to_parallel_data_1_disp_en), .CLK(CLK_IN),
    .PARALLEL_IN(serial_to_parallel_data_1_parallel_out), .DISPLAY_OUT(OUT));
  Seven_Seg seven_seg_1 (
    .a(OUT[15]), .b(OUT[14]), .c(OUT[13]), .d(OUT[12]), .e(OUT[11]), .f(OUT[10]), .g(OUT[9]), .dp(OUT[8]));
  Seven_Seg seven_seg_2 (
    .a(OUT[7]), .b(OUT[6]), .c(OUT[5]), .d(OUT[4]), .e(OUT[3]), .f(OUT[2]), .g(OUT[1]), .dp(OUT[0]));

  // Notes on the sheet:
  //   B: default 1
  //   START: default 1
  //   SERIAL: default 1
endmodule

/* Test case TEST CASE:
CLK_IN	A	B	START	SERIAL	OUT
1	0	1	0	1	0xFCFC
0	0	1	0	1	0xFCFC
1	0	1	0	1	0xFCFC
0	0	1	0	1	0xFCFC
1	0	1	0	1	0xFCFC
0	0	1	0	1	0xFCFC
1	0	1	0	1	0xFCFC
0	0	1	0	1	0xFCFC
1	0	1	0	1	0xFCFC
0	0	1	0	1	0xFCFC
1	0	1	0	1	0xFCFC
0	0	1	0	1	0xFCFC
1	0	1	0	1	0xFCFC
0	0	1	0	1	0xFCFC
1	0	1	0	1	0xFCFC
0	0	1	0	1	0xFCFC
1	0	1	0	1	0xFCFC
0	0	1	0	1	0xFCFC
1	0	1	0	0	0xFCFC
0	0	1	0	0	0xFCFC
1	0	1	0	0	0xFCFC
0	0	1	0	0	0xFCFC
1	0	1	0	0	0xFCFC
0	0	1	0	0	0xFCFC
1	0	1	0	0	0xFCFC
0	0	1	0	0	0xFCFC
1	0	1	0	1	0xFCFC
0	0	1	0	1	0xFCFC
1	0	1	0	1	0xFCFC
0	0	1	0	1	0xFCFC
1	0	1	0	1	0xFCFC
0	0	1	0	1	0xFCFC
1	0	1	0	1	0xFCFC
0	0	1	0	1	0xFCFC
1	0	1	0	0	0xFCFC
0	0	1	0	0	0xFCFC
1	0	1	0	0	0xFCFC
0	0	1	0	0	0xFCFC
1	0	1	0	0	0xFCFC
0	0	1	0	0	0xFCFC
1	0	1	0	0	0xFCFC
0	0	1	0	0	0xFCFC
1	0	1	0	0	0xFCFC
0	0	1	0	0	0xFCFC
1	0	1	0	0	0xFCFC
0	0	1	0	0	0xFCFC
1	0	1	0	0	0xFCFC
0	0	1	0	0	0xFCFC
1	0	1	0	0	0xFCFC
0	0	1	0	0	0xFCFC
1	0	1	0	1	0xFCFC
0	0	1	0	1	0xFCFC
1	0	1	0	1	0xFCFC
0	0	1	0	1	0xFCFC
1	0	1	0	1	0xFCFC
0	0	1	0	1	0xFCFC
1	0	1	0	1	0xFCFC
0	0	1	0	1	0xFCFC
1	0	1	0	0	0xF6E0
*/
