// Digital circuit display buffer.dig as structural Verilog
module display_buffer (
  input  ENABLE,
  input  CLK,
  input  [15:0] PARALLEL_IN,
  output [15:0] DISPLAY_OUT
);

  Register #(.Bits(16)) register_1 (.D(PARALLEL_IN), .C(CLK), .en(ENABLE), .Q(DISPLAY_OUT));
  Seven_Seg seven_seg_1 (
    .a(DISPLAY_OUT[15]), .b(DISPLAY_OUT[14]), .c(DISPLAY_OUT[13]), .d(DISPLAY_OUT[12]), .e(DISPLAY_OUT[11]),
    .f(DISPLAY_OUT[10]), .g(DISPLAY_OUT[9]), .dp(DISPLAY_OUT[8]));
  Seven_Seg seven_seg_2 (
    .a(DISPLAY_OUT[7]), .b(DISPLAY_OUT[6]), .c(DISPLAY_OUT[5]), .d(DISPLAY_OUT[4]), .e(DISPLAY_OUT[3]),
    .f(DISPLAY_OUT[2]), .g(DISPLAY_OUT[1]), .dp(DISPLAY_OUT[0]));
endmodule

/* Test case:
CLK	PARALLEL_IN	ENABLE	DISPLAY_OUT
1	0xFCFC	1	0xFCFC
0	0xFCFC	1	0xFCFC
1	0xE0FC	1	0xE0FC
0	0xE0FC	1	0xE0FC
1	0xFEFC	1	0xFEFC
0	0xFEFC	1	0xFEFC
1	0xB660	1	0xB660
0	0xB660	1	0xB660
*/
