// Digital circuit serial to parallel data.dig as structural Verilog
module serial_to_parallel_data (
  input  START,
  input  CLK,
  input  SERIAL_IN,
  output [15:0] PARALLEL_OUT,
  output DISP_EN
);

  wire _74164_1_pin3, _74164_1_pin4, _74164_1_pin5, _74164_1_pin6, _74164_1_pin9, _74164_1_pin10,
       _74164_1_pin11, _74164_1_pin12, _74164_1_pin13;

  LookUpTable #(.Bits(8)) lookuptable_1 (
    .in0(_74164_1_pin6), .in1(_74164_1_pin5), .in2(_74164_1_pin4), .in3(_74164_1_pin3),
    .out(PARALLEL_OUT[15:8]));
  _74164 _74164_1 (
    .pin1(SERIAL_IN), .pin2(SERIAL_IN), .pin3(_74164_1_pin3), .pin4(_74164_1_pin4), .pin5(_74164_1_pin5),
    .pin6(_74164_1_pin6), .pin7(1'b0), .pin8(CLK), .pin9(_74164_1_pin9), .pin10(_74164_1_pin10),
    .pin11(_74164_1_pin11), .pin12(_74164_1_pin12), .pin13(_74164_1_pin13), .pin14(1'b1));
  LookUpTable #(.Bits(8)) lookuptable_2 (
    .in0(_74164_1_pin13), .in1(_74164_1_pin12), .in2(_74164_1_pin11), .in3(_74164_1_pin10),
    .out(PARALLEL_OUT[7:0]));
  not not_1 (_74164_1_pin9, START);
  Enable_Counter enable_counter_1 (.CLK(CLK), .DISP_EN(DISP_EN));

  // Notes on the sheet:
  //   contents of lookuptable_1 (hex, n*v repeats v):
  //   fc,60,da,f2,66,b6,be,e0,fe,f6,6*1
  //   contents of lookuptable_2 (hex, n*v repeats v):
  //   fc,60,da,f2,66,b6,be,e0,fe,f6,6*1
endmodule

/* Test case:
CLK	START	SERIAL_IN	PARALLEL_OUT	DISP_EN
0	0	1	0xFCFC	1
1	0	1	0xFEFC	0
0	0	1	0xFEFC	0
1	0	1	0x1FC	0
0	0	1	0x1FC	0
1	0	0	0x1FC	0
0	0	0	0x1FC	0
1	0	1	0xE0FC	0
0	0	1	0xE0FC	0
1	0	0	0x1FE	0
0	0	0	0x1FE	0
1	0	0	0xB601	0
0	0	0	0xB601	0
1	0	1	0xDA01	0
0	0	1	0xDA01	0
1	0	0	0xF6E0	1
*/
